# Fritzing sketch Pass Center (saved by Fritzing 0.9.3b)
breadboards: 1

parts:
  Componente1 = LCD1602-I2C
  Componente2 = RFID-RC522 [part_number=101218]
  S1 = Momentary Switch [package=ksa_sealed_tac_switch]
  R1 = Resistor [tolerance=±5% resistance=220 package="2010 [SMD]"]
  U1 = LuaNode32 / ESP32

nets:
  GND: Componente1.GND, Componente2.GND, R1.Pin_0, U1.GND
  VCC: Componente1.VCC, U1.Vin
  N1: Componente1.SDA, U1.D21
  N2: Componente1.SCL, U1.D22
  N3: Componente2.SDA, U1.D5
  N4: Componente2.SCK, U1.D18
  N5: Componente2.MOSI, U1.D23
  N6: Componente2.MISO, U1.D19
  N7: Componente2.RST, U1.VP
  3.3V: Componente2.3.3V, S1.2, U1.3V3
  N8: S1.4, R1.Pin_1, U1.D2

custom parts:
  LCD1602-I2C: A standard character display, usually with 2x16 characters. Comes in many colors with LCM1602 IIC attached.
  LuaNode32 / ESP32: ESP32 based LuaNode32
